# Fritzing sketch die-layout (saved by Fritzing 0.9.2b)
breadboards: 1

parts:
  Part1 = Arduino Nano (Rev3.0)
  LED1 = LED - 5mm [color="Green (565nm)" package="5 mm [THT]"]
  LED2 = LED - 5mm [color="Green (565nm)" package="5 mm [THT]"]
  LED3 = LED - 5mm [color="Green (565nm)" package="5 mm [THT]"]
  LED4 = LED - 5mm [color="Green (565nm)" package="5 mm [THT]"]
  LED5 = LED - 5mm [color="Green (565nm)" package="5 mm [THT]"]
  LED6 = LED - 5mm [color="Green (565nm)" package="5 mm [THT]"]
  LED7 = LED - 5mm [color="Green (565nm)" package="5 mm [THT]"]
  R1 = Resistor [tolerance=±5% resistance=150 package=THT]
  R2 = Resistor [tolerance=±5% resistance=150 package=THT]
  R3 = Resistor [tolerance=±5% resistance=150 package=THT]
  R4 = Resistor [tolerance=±5% resistance=150 package=THT]
  R5 = Resistor [tolerance=±5% resistance=150 package=THT]
  R6 = Resistor [tolerance=±5% resistance=150 package=THT]
  R7 = Resistor [tolerance=±5% resistance=150 package=THT]
  S1 = Pushbutton [package=THT]
  R8 = Resistor [tolerance=±5% resistance=10k package=THT]

nets:
  N1: Part1.GND, R1.Pin_1, R2.Pin_1, R3.Pin_1, R4.Pin_1, R5.Pin_1, R6.Pin_1, R7.Pin_1, R8.Pin_1
  N2: Part1.D5, S1.leg0, R8.Pin_0
  N3: Part1.D7, LED4.anode
  N4: Part1.D8, LED1.anode
  N5: Part1.D9, LED2.anode
  N6: Part1.D10, LED3.anode
  N7: Part1.D11/MOSI, LED5.anode
  N8: Part1.D12/MISO, LED6.anode
  N9: Part1.5V, S1.leg1
  N10: Part1.D13/SCK, LED7.anode
  N11: LED1.cathode, R1.Pin_0
  N12: LED2.cathode, R2.Pin_0
  N13: LED3.cathode, R3.Pin_0
  N14: LED4.cathode, R4.Pin_0
  N15: LED5.cathode, R7.Pin_0
  N16: LED6.cathode, R6.Pin_0
  N17: LED7.cathode, R5.Pin_0
